# Fritzing sketch wiring-fritzing (saved by Fritzing 1.0.2b)
circuit board: 8.46667cm x 5.64444cm
breadboards: 1

parts:
  Mod1 = Raspberry Pi Pico
  Part1 = Adafruit RFM9x LoRa Radio [part_number="Adafruit #3072 and #3073"]

nets:
  N1: Mod1.pin_3, Mod1.pin_8, Mod1.pin_13, Mod1.pin_18, Mod1.pin_23, Mod1.pin_28, Mod1.pin_33, Mod1.pin_38, Part1.GND
  N2: Mod1.pin_21, Part1.MISO
  N3: Mod1.pin_22, Part1.CS
  N4: Mod1.pin_24, Part1.SCK
  N5: Mod1.pin_25, Part1.MOSI
  N6: Mod1.pin_26, Part1.RST
  N7: Mod1.pin_36, Part1.VIN

custom parts:
  Raspberry Pi Pico: Raspberry Pi Pico. Based around the RP2040 microcontroller the Pico is a low cost microcontroller device bringing Raspberry Pi quality, cost, and easy of use to the microcontroller space. Jan 2021, Split part in to two versions: tht (this one) and SMD. This one will drill holes for a .1 in header in pcb to allow plugging in the module as well as providing pads to solder the module to the top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
  Adafruit RFM9x LoRa Radio: Sending data over long distances is like magic, and now you can be a magician with this range of powerful and easy-to-use radio modules. Sure, sometimes you want to talk to a computer (a good time to use WiFi) or perhaps communicate with a Phone (choose Bluetooth Low Energy!) but what if you want to send data very far? Most WiFi, Bluetooth, Zigbee and other wireless chipsets use 2.4GHz, which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
